# Fritzing sketch protoboard-flash (saved by Fritzing 0.9.3b)
breadboards: 1

parts:
  Part1 = FTDI Basic Programmer
  U2 = ESP8266 WiFi Module [part_number=ESP8266]

nets:
  N1: Part1.RXI, U2.TXD
  N2: Part1.TXO, U2.RXD
